// Digital circuit 3102-week2.dig as structural Verilog
module _3102_week2 (
  input  a0,
  input  b0,
  input  a1,
  input  b1,
  input  a2,
  input  b2,
  input  a3,
  input  b3,
  output out_9
);

  wire and_1_out, and_2_out, and_3_out, and_4_out, and_5_out, and_6_out, and_7_out, and_8_out, and_9_out,
       not_1_out, not_2_out, not_3_out, not_4_out, or_1_out, or_2_out, or_3_out, or_4_out, or_5_out;

  not not_1 (not_1_out, b0);
  not not_2 (not_2_out, b1);
  not not_3 (not_3_out, b2);
  not not_4 (not_4_out, b3);
  and and_1 (and_1_out, a0, not_1_out);
  or or_1 (or_1_out, a0, not_1_out);
  and and_2 (and_2_out, a1, not_2_out);
  or or_2 (or_2_out, a1, not_2_out);
  and and_3 (and_3_out, a2, not_3_out);
  or or_3 (or_3_out, a2, not_3_out);
  and and_4 (and_4_out, a3, not_4_out);
  and and_5 (and_5_out, or_1_out, and_2_out);
  and and_6 (and_6_out, or_1_out, or_2_out);
  or or_4 (or_4_out, and_1_out, and_5_out);
  and and_7 (and_7_out, and_6_out, and_3_out);
  and and_8 (and_8_out, and_6_out, or_3_out);
  or or_5 (or_5_out, or_4_out, and_7_out);
  and and_9 (and_9_out, and_8_out, and_4_out);
  or or_6 (out_9, or_5_out, and_9_out);
endmodule
