// Digital circuit add4.dig as structural Verilog
module add4 (
  input  a_3,
  input  b_3,
  input  a_0,
  input  b_0,
  input  a_1,
  input  b_1,
  input  a_2,
  input  b_2,
  output out_4,
  output out_3,
  output out_2,
  output out_1,
  output out_0
);

  wire fadd_1_c_out, fadd_2_c_out, fadd_3_c_out;

  fadd fadd_1 (.a(a_3), .b(b_3), .c_in(1'b0), .sum(out_4), .c_out(fadd_1_c_out));
  fadd fadd_2 (.a(a_2), .b(b_2), .c_in(fadd_1_c_out), .sum(out_3), .c_out(fadd_2_c_out));
  fadd fadd_3 (.a(a_1), .b(b_1), .c_in(fadd_2_c_out), .sum(out_2), .c_out(fadd_3_c_out));
  fadd fadd_4 (.a(a_0), .b(b_0), .c_in(fadd_3_c_out), .sum(out_1), .c_out(out_0));
endmodule
