// Digital circuit fadd.dig as structural Verilog
module fadd (
  input  a,
  input  b,
  input  c_in,
  output sum,
  output c_out
);

  wire nand_1_out, nand_2_out, nand_3_out, nand_4_out, nand_5_out, nand_6_out, nand_7_out;

  nand nand_1 (nand_1_out, a, b);
  nand nand_2 (nand_2_out, a, nand_1_out);
  nand nand_3 (nand_3_out, nand_1_out, b);
  nand nand_4 (nand_4_out, nand_2_out, nand_3_out);
  nand nand_5 (nand_5_out, nand_4_out, c_in);
  nand nand_6 (nand_6_out, nand_4_out, nand_5_out);
  nand nand_7 (nand_7_out, nand_5_out, c_in);
  nand nand_8 (sum, nand_6_out, nand_7_out);
  nand nand_9 (c_out, nand_5_out, nand_1_out);
endmodule
