// Digital circuit mult4.dig as structural Verilog
module mult4 (
  input  a_0,
  input  a_1,
  input  a_2,
  input  a_3,
  input  b_0,
  input  b_1,
  input  b_2,
  input  b_3,
  output out_0,
  output out_1,
  output out_2,
  output out_3,
  output out_4,
  output out_5,
  output out_6,
  output out_7
);

  wire add4_1_out_0, add4_1_out_1, add4_1_out_2, add4_1_out_3, add4_2_out_0, add4_2_out_1, add4_2_out_2,
       add4_2_out_3, mult41_1_out_0, mult41_1_out_1, mult41_1_out_2, mult41_1_out_3, mult41_2_out_0,
       mult41_2_out_1, mult41_2_out_2, mult41_2_out_3, mult41_3_out_0, mult41_3_out_1, mult41_3_out_2,
       mult41_3_out_3, mult41_4_out_0, mult41_4_out_1, mult41_4_out_2;

  mult41 mult41_1 (
    .a_0(a_0), .a_1(a_1), .a_2(a_2), .a_3(a_3), .b_0(b_0), .out_1(mult41_1_out_1), .out_0(mult41_1_out_0),
    .out_2(mult41_1_out_2), .out_3(mult41_1_out_3));
  mult41 mult41_2 (
    .a_0(a_0), .a_1(a_1), .a_2(a_2), .a_3(a_3), .b_0(b_1), .out_1(mult41_2_out_1), .out_0(mult41_2_out_0),
    .out_2(mult41_2_out_2), .out_3(mult41_2_out_3));
  mult41 mult41_3 (
    .a_0(a_0), .a_1(a_1), .a_2(a_2), .a_3(a_3), .b_0(b_2), .out_1(mult41_3_out_1), .out_0(mult41_3_out_0),
    .out_2(mult41_3_out_2), .out_3(mult41_3_out_3));
  mult41 mult41_4 (
    .a_0(a_0), .a_1(a_1), .a_2(a_2), .a_3(a_3), .b_0(b_3), .out_1(mult41_4_out_1), .out_0(mult41_4_out_0),
    .out_2(mult41_4_out_2), .out_3(out_7));
  add4 add4_1 (
    .a_3(mult41_3_out_3), .b_3(mult41_4_out_2), .a_0(mult41_3_out_0), .b_0(1'b0), .a_1(mult41_3_out_1),
    .b_1(mult41_4_out_0), .a_2(mult41_3_out_2), .b_2(mult41_4_out_1), .out_4(out_6), .out_3(add4_1_out_3),
    .out_2(add4_1_out_2), .out_1(add4_1_out_1), .out_0(add4_1_out_0));
  add4 add4_2 (
    .a_3(mult41_2_out_3), .b_3(add4_1_out_3), .a_0(mult41_2_out_0), .b_0(add4_1_out_0), .a_1(mult41_2_out_1),
    .b_1(add4_1_out_1), .a_2(mult41_2_out_2), .b_2(add4_1_out_2), .out_4(out_5), .out_3(add4_2_out_3),
    .out_2(add4_2_out_2), .out_1(add4_2_out_1), .out_0(add4_2_out_0));
  add4 add4_3 (
    .a_3(mult41_1_out_3), .b_3(add4_2_out_3), .a_0(mult41_1_out_0), .b_0(add4_2_out_0), .a_1(mult41_1_out_1),
    .b_1(add4_2_out_1), .a_2(mult41_1_out_2), .b_2(add4_2_out_2), .out_4(out_4), .out_3(out_3),
    .out_2(out_2), .out_1(out_1), .out_0(out_0));
endmodule
