// Digital circuit mult41.dig as structural Verilog
module mult41 (
  input  a_0,
  input  a_1,
  input  a_2,
  input  a_3,
  input  b_0,
  output out_1,
  output out_0,
  output out_2,
  output out_3
);

  wire nand_1_out, nand_2_out, nand_3_out, nand_4_out;

  nand nand_1 (nand_1_out, a_0, b_0);
  nand nand_2 (nand_2_out, a_1, b_0);
  nand nand_3 (nand_3_out, a_2, b_0);
  nand nand_4 (nand_4_out, a_3, b_0);
  nand nand_5 (out_0, nand_1_out, nand_1_out);
  nand nand_6 (out_1, nand_2_out, nand_2_out);
  nand nand_7 (out_2, nand_3_out, nand_3_out);
  nand nand_8 (out_3, nand_4_out, nand_4_out);
endmodule
